# Fritzing sketch CyGarage (saved by Fritzing 0.9.3b)
circuit board: 8.46667cm x 5.64444cm
breadboards: 1

parts:
  LED2 = LED - 5mm [color="Red (633nm)" package="5 mm [THT]"]
  LED1 = LED - 5mm [color="Green (555nm)" package="5 mm [THT]"]
  J1 = Screw terminal - 2 pins [package=THT]
  J3 = Screw terminal - 2 pins [package=THT]
  J2 = Screw terminal - 2 pins [package=THT]
  Adafruit_HUZZAH_ESP8266_Breakout = Adafruit HUZZAH ESP8266 Breakout [part_number=2471]
  R1 = Resistor [tolerance=±5% resistance=330 package=THT]
  R2 = Resistor [tolerance=±5% resistance=330 package=THT]
  DC1 = Reed switch [package=THT]  # not connected
  DC2 = Reed switch [package=THT]  # not connected
  Part1 = Adafruit PowerRelay Feather Wing [part_number="Adafruit #3191"]

nets:
  N1: LED2.cathode, LED1.cathode
  N2: LED2.anode, Adafruit_HUZZAH_ESP8266_Breakout.#5
  N3: LED1.anode, Adafruit_HUZZAH_ESP8266_Breakout.#2
  GND: J1.pin1, J3.pin1, J2.pin2, Adafruit_HUZZAH_ESP8266_Breakout.GND, Part1.GND
  N4: J1.pin2, Adafruit_HUZZAH_ESP8266_Breakout.V+, R1.Pin_1, R2.Pin_1
  N5: J3.pin2, Adafruit_HUZZAH_ESP8266_Breakout.#13, R2.Pin_0
  N6: J2.pin1, Adafruit_HUZZAH_ESP8266_Breakout.#12, R1.Pin_0
  N7: Adafruit_HUZZAH_ESP8266_Breakout.#4, Part1.A
  N8: Adafruit_HUZZAH_ESP8266_Breakout.3V, Part1.3.3V

custom parts:
  Adafruit PowerRelay Feather Wing: A Feather board without ambition is a Feather board without FeatherWings! This is the Power Relay FeatherWing. It gives you power to control, and control over power. Put simply, you can now turn on and off lamps, fans, solenoids, and other small appliances that run on up to 250VAC or DC power using any Feather board. Compared to our smaller Relay FeatherWings, this one can handle a beefy 1200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
